// Logisim project ALU_4bit_Upgraded.circ as structural Verilog: 1 circuit, main circuit main
module main (
  input  [3:0] A,
  input  [3:0] B,
  input  S2,
  input  S1,
  input  S0,
  input  LOAD,
  output CARRY,
  output [3:0] RESULT,
  output [3:0] STORED,
  output BORROW,
  output ZERO,
  output EQUAL,
  output GREATER,
  output LESS
);

  wire and_2_out, and_3_out, BW_SUB, C_ADD, C_INC, CLK, CLR, EQ, GT, LT, OP_ADD, OP_AND, OP_CMP, OP_INC,
       OP_NOT, OP_OR, OP_SUB, OP_XOR, SF_B, SF_C, SF_EQ, SF_GT, SF_LT, SF_Z;
  wire [3:0] multiplexer_2_out, R_ADD, R_AND, R_INC, R_NOT, R_OR, R_SUB, R_XOR;

  Button u_CLK (.out(CLK));
  Button u_CLR (.out(CLR));
  Hex_Digit_Display hex_digit_display_1 (.value(A));  // open: dp
  Hex_Digit_Display hex_digit_display_2 (.value(B));  // open: dp
  LED LED_ADD (.in(OP_ADD));
  LED LED_SUB (.in(OP_SUB));
  LED LED_AND (.in(OP_AND));
  LED LED_OR (.in(OP_OR));
  LED LED_XOR (.in(OP_XOR));
  LED LED_NOT (.in(OP_NOT));
  LED LED_INC (.in(OP_INC));
  LED LED_CMP (.in(OP_CMP));
  Hex_Digit_Display hex_digit_display_3 (.value(RESULT));  // open: dp
  Hex_Digit_Display hex_digit_display_4 (.value(STORED));  // open: dp
  LED LV_CARRY (.in(CARRY));
  LED LV_BORROW (.in(BORROW));
  LED LV_ZERO (.in(ZERO));
  LED LV_EQUAL (.in(EQUAL));
  LED LV_GREATER (.in(GREATER));
  LED LV_LESS (.in(LESS));
  LED ST_CARRY (.in(SF_C));
  LED ST_BORROW (.in(SF_B));
  LED ST_ZERO (.in(SF_Z));
  LED ST_EQUAL (.in(SF_EQ));
  LED ST_GREATER (.in(SF_GT));
  LED ST_LESS (.in(SF_LT));
  assign R_AND = A & B;  // AND_Gate and_1, 4 bits wide
  assign R_OR = A | B;  // OR_Gate or_1, 4 bits wide
  assign R_XOR = A ^ B;  // XOR_Gate xor_1, 4 bits wide
  assign R_NOT = ~A;  // NOT_Gate not_1, 4 bits wide
  Adder #(.width(4)) adder_1 (.a(A), .b(B), .out(R_ADD), .cin(1'b0), .cout(C_ADD));
  Subtractor #(.width(4)) subtractor_1 (.a(A), .b(B), .out(R_SUB), .bin(1'b0), .bout(BW_SUB));
  Adder #(.width(4)) adder_2 (.a(A), .b(4'b0001), .out(R_INC), .cin(1'b0), .cout(C_INC));
  Comparator #(.mode("unsigned"), .width(4)) comparator_1 (.a(A), .b(B), .gt(GT), .eq(EQ), .lt(LT));
  Decoder #(.enable("false"), .select(3)) decoder_1 (
    .out0(OP_ADD), .out1(OP_SUB), .out2(OP_AND), .out3(OP_OR), .out4(OP_XOR), .out5(OP_NOT), .out6(OP_INC),
    .out7(OP_CMP), .sel({S2, S1, S0}));
  Multiplexer #(.select(3), .width(4)) multiplexer_1 (
    .in0(R_ADD), .in1(R_SUB), .in2(R_AND), .in3(R_OR), .in4(R_XOR), .in5(R_NOT), .in6(R_INC),
    .in7({1'b0, LT, EQ, GT}), .out(RESULT), .sel({S2, S1, S0}));
  and and_2 (and_2_out, OP_ADD, C_ADD);
  and and_3 (and_3_out, OP_INC, C_INC);
  and and_4 (BORROW, OP_SUB, BW_SUB);
  and and_5 (EQUAL, OP_CMP, EQ);
  and and_6 (GREATER, OP_CMP, GT);
  and and_7 (LESS, OP_CMP, LT);
  or or_2 (CARRY, and_2_out, and_3_out);
  nor nor_1 (ZERO, RESULT[0], RESULT[1], RESULT[2], RESULT[3]);
  Multiplexer #(.width(4)) multiplexer_2 (.in0(STORED), .in1(RESULT), .out(multiplexer_2_out), .sel(LOAD));
  D_Flip_Flop d_ff_1 (.D(multiplexer_2_out[0]), .clk(CLK), .Q(STORED[0]), .preset(1'b0), .reset(CLR));  // open: Qn
  D_Flip_Flop d_ff_2 (.D(multiplexer_2_out[1]), .clk(CLK), .Q(STORED[1]), .preset(1'b0), .reset(CLR));  // open: Qn
  D_Flip_Flop d_ff_3 (.D(multiplexer_2_out[2]), .clk(CLK), .Q(STORED[2]), .preset(1'b0), .reset(CLR));  // open: Qn
  D_Flip_Flop d_ff_4 (.D(multiplexer_2_out[3]), .clk(CLK), .Q(STORED[3]), .preset(1'b0), .reset(CLR));  // open: Qn
  Register #(.width(6)) STATUS (
    .D({LESS, GREATER, EQUAL, ZERO, BORROW, CARRY}), .en(LOAD), .clk(CLK),
    .Q({SF_LT, SF_GT, SF_EQ, SF_Z, SF_B, SF_C}), .clr(CLR));

  // Other names for the same wires on the sheet: F_C = CARRY; F_B = BORROW; F_Z = ZERO; F_EQ = EQUAL; F_GT = GREATER;
  //   F_LT = LESS; Q[3:0] = STORED; R_CMP[2:0] = {LT, EQ, GT}; Y[3:0] = RESULT

  // Notes on the sheet:
  //   A: initial=0x5
  //   B: initial=0x3
  //   UPGRADED 4-BIT ALU  -  8 OPERATIONS, RESULT REGISTER (D flip-flops) AND STATUS FLAGS
  //   CONTROL INPUTS
  //   OPERATION CODES  S2 S1 S0
  //   000  ADD  A + B     -> Carry
  //   001  SUB  A - B     -> Borrow
  //   010  AND  A AND B
  //   011  OR   A OR B
  //   100  XOR  A XOR B
  //   101  NOT  NOT A
  //   110  INC  A + 1     -> Carry
  //   111  CMP  A vs B    -> EQ/GT/LT
  //   CMP result code on Y:
  //     0001 = A>B  0010 = A=B
  //     0100 = A<B
  //   ZERO = 1 when live Y = 0000
  //   operand A (click bits)
  //   operand B (click bits)
  //   LOAD = 1 : store on next CLK
  //   CLK : click = one clock pulse
  //   CLR : click = clear registers
  //   operation select
  //   (S2 S1 S0)
  //   OUTPUT DISPLAYS
  //   A
  //   SELECTED OPERATION
  //   B
  //   000  ADD
  //   001  SUB
  //   010  AND
  //   011  OR
  //   100  XOR
  //   101  NOT
  //   110  INC
  //   111  CMP
  //   LIVE Y
  //   <- live ALU output (combinational)
  //   <- stored register output
  //   STATUS FLAGS
  //   STORED Q
  //   live
  //   stored
  //   CARRY
  //   BORROW
  //   ZERO
  //   EQUAL
  //   GREATER
  //   LESS
  //   ARITHMETIC & LOGIC UNITS (all compute in parallel)
  //   ADDER  A+B
  //   SUBTRACTOR  A-B
  //   AND (bitwise)
  //   OR (bitwise)
  //   XOR (bitwise)
  //   NOT A
  //   INCREMENTER  A+1
  //   COMPARATOR
  //   CMP encoder
  //   Y = 0 LT EQ GT
  //   000
  //   001
  //   010
  //   011
  //   100
  //   101
  //   110
  //   111
  //   OPERATION SELECTION
  //   8:1 MUX (4-bit)
  //   3-to-8 DECODER
  //   Y
  //   STATUS FLAG LOGIC
  //   CARRY = (ADD . Cout) + (INC . Cout)
  //   EQUAL / GREATER / LESS = CMP . comparator output
  //   BORROW = SUB . Bout
  //   ZERO = NOR(Y3..Y0)
  //   RESULT REGISTER  (4 x D flip-flop + LOAD multiplexer)
  //   STATUS REGISTER (6-bit, stores flags with LOAD)
  //   0 = hold Q
  //   1 = load Y
  //   LOAD MUX
  //   bit 0
  //   bit 1
  //   bit 2
  //   bit 3
  //   Q = stored
  //   result
endmodule
